# Fritzing sketch Potenciometro (saved by Fritzing 0.9.2b)
breadboards: 1

parts:
  Componente1 = Arduino Uno (Rev3) - ICSP
  U1 = POT [package=pot_mammoth]

nets:
  N1: Componente1.A5/SCL, U1.A
  N2: Componente1.5V, U1.E
  N3: Componente1.GND, U1.S

// code stored in the sketch: Potenciometro.ino
/*
 * Entrada analógica
 * por DojoDave <http://www.0j0.org>
 *
 * Liga e desliga um LED conectado ao pino digital 13. O tempo
 * que o LED permanece ligado ou desligado depende do valor
 * obtido pelo analogRead(). No caso mais simples, conectamos
 * um potenciômetro ao pino analógico 2.
 */

int potPin = 5;    // selecione o pino de entrada ao potenciômetro
int ledPin = 13;   // selecione o pino ao LED
int val = 0;       // variável a guardar o valor proveniente do sensor

void setup() {
  pinMode(ledPin, OUTPUT);  // declarar o pino ledPin como saída
}

void loop() {
  val = analogRead(potPin);    // ler o valor do potenciômetro
  digitalWrite(ledPin, HIGH);  // ligar o ledPin
  delay(val);                  // pausar o programa por algum tempo
  digitalWrite(ledPin, LOW);   // desligar o ledPin
  delay(val);                  // pausar o programa por algum tempo
}
